# Fritzing sketch Sema (saved by Fritzing 0.9.4)
breadboards: 1

parts:
  FET1 = STP16NF06 N-Channel Power MOSFET
  FET2 = STP16NF06 N-Channel Power MOSFET
  Parça1 = Arduino Nano (Rev3.0) (ICSP)
  J1 = Power Jack [package=power_jack_smd]
  JP1 = RCA [package=rca_lock]
  R1 = Resistor [tolerance=±5% resistance=220 package="1206 [SMD]"]
  LED1 = LEDs [package=led10mm]
  R2 = Rotary Potentiometer (Small) [maximum_resistance=100kΩ package=THT]

nets:
  N1: FET1.drain, FET2.drain, JP1.SHELL
  GND: FET1.source, FET2.source, Parça1.GND, J1.GND, R1.Pin_1, R2.leg1
  N2: FET2.gate, Parça1.D3
  N3: Parça1.D10, LED1.A
  N4: Parça1.VIN, J1.GNDBREAK, JP1.PIN
  N5: Parça1.5V, R2.leg2
  N6: Parça1.A5, R2.wiper
  N7: R1.Pin_0, LED1.C

notes:
  ırfz44n

custom parts:
  STP16NF06 N-Channel Power MOSFET: STP16NF06 N-channel Power MOSFET
